# Fritzing sketch SDKard.ca2019-07-18s (saved by Fritzing 0.9.3b)
circuit board: 6.5cm x 11.5cm
breadboards: 1

parts:
  u1 = BluePill
  J3 = female pin header, 8 pins [form="♀ (female)"]
  J4 = female pin header, 8 pins [form="♀ (female)"]
  J5 = female pin header, 2 pins [form="♀ (female)"]
  J2 = female pin header, 10 pins [form="♀ (female)"]
  J1 = female pin header, 8 pins [form="♀ (female)"]
  BME = female pin header, 4 pins [form="♀ (female)"]
  232R = female pin header, 6 pins [form="♀ (female)"]
  VL53 = female pin header, 4 pins [form="♀ (female)"]
  PCF = female pin header, 4 pins [form="♀ (female)"]

nets:
  N1: u1.A0, J4.pin1
  N2: u1.A1, J4.pin2
  N3: u1.A3, J4.pin4
  N4: u1.A4, J4.pin5
  N5: u1.A5, J4.pin6
  N6: u1.A6, J4.pin7
  N7: u1.A7, J4.pin8
  N8: u1.B0, J5.pin1
  N9: u1.B10, J2.pin10, BME.pin4, VL53.pin3, PCF.pin4
  N10: u1.B11, J2.pin9, BME.pin3, VL53.pin4, PCF.pin3
  N11: u1.NRST, J3.pin3
  N12: u1.3V3, BME.pin2
  GND: u1.GND, u1.GND2, J2.pin7, BME.pin1, 232R.pin6
  N13: u1.3V31, J3.pin4, VL53.pin1, PCF.pin1
  N14: u1.GND3, J3.pin6, J3.pin7, VL53.pin2, PCF.pin2
  N15: u1.5V, J3.pin5
  N16: u1.B9, J2.pin2
  N17: u1.B8, J2.pin1
  N18: u1.B7, J1.pin8
  N19: u1.B6, J1.pin7
  N20: u1.A15, J1.pin6
  N21: u1.A10, J1.pin5, 232R.pin3
  N22: u1.A9, J1.pin4, 232R.pin2
  N23: u1.A8, J1.pin3
  N24: u1.B15, J2.pin4
  N25: u1.B14, J2.pin5
  N26: u1.B13, J2.pin6
  N27: u1.B12, J2.pin3
  N28: u1.B1, J5.pin2
  N29: u1.A2, J4.pin3

notes:
  PA0
  G
  R
  MAX3.3
  3.3
  5V
  JTDI
  RX1
  TX1
  ~PA0
  ~PA1
  ~PB0
  ~PB1
  ~PA7
  ~PA6
  PA5
  PA4
  ~PA3
  ~PA2
  -----------3.3 V MAX-----
  TX
  RX
  ~PA8
  ~PA9
  ~PA10
  ~PA15
  ~PB6
  ~PB7
  ~PB8
  ~PB9
  PB12
  PB15
  PB14
  PB13
  G G3.3
  5V G3.3
  SCK2
  MISO2
  MOSI2
  NSS2
  CANRX
  CANTX
  PB11
  SDA2
  PB10
  SCL2
  SDKard.ca2019-07-18s
  KM
